// Digital circuit COMPUTER.dig as structural Verilog
module COMPUTER (
  input  A7,
  input  A6,
  input  A5,
  input  A4,
  input  A3,
  input  A2,
  input  A1,
  input  A0,
  input  B0,
  input  B1,
  input  B2,
  input  B3,
  input  B4,
  input  B5,
  input  B6,
  input  B7,
  input  PROGRAM,
  input  clk,
  input  CLK_MODE,
  input  CLK_2
);

  wire _00_PXL, _01_PXL, _02_PXL, _03_PXL, _04_PXL, _05_PXL, _06_PXL, _07_PXL, _10_PXL, _11_PXL, _12_PXL,
       _13_PXL, _14_PXL, _15_PXL, _16_PXL, _17_PXL, _20_PXL, _21_PXL, _22_PXL, _23_PXL, _24_PXL, _25_PXL,
       _26_PXL, _27_PXL, _30_PXL, _31_PXL, _32_PXL, _33_PXL, _34_PXL, _35_PXL, _36_PXL, _37_PXL, _40_PXL,
       _41_PXL, _42_PXL, _43_PXL, _44_PXL, _45_PXL, _46_PXL, _47_PXL, _50_PXL, _51_PXL, _52_PXL, _53_PXL,
       _54_PXL, _55_PXL, _56_PXL, _57_PXL, multiplexer_1_out;
  wire [7:0] add_8_1_s, Address_q, DATA_d;
  wire [15:0] INSTR_d;

  LED led_1 (.in(_07_PXL));
  LED led_2 (.in(_06_PXL));
  LED led_3 (.in(_17_PXL));
  LED led_4 (.in(_16_PXL));
  LED led_5 (.in(_27_PXL));
  LED led_6 (.in(_26_PXL));
  LED led_7 (.in(_37_PXL));
  LED led_8 (.in(_36_PXL));
  LED led_9 (.in(_47_PXL));
  LED led_10 (.in(_46_PXL));
  LED led_11 (.in(_57_PXL));
  LED led_12 (.in(_56_PXL));
  LED led_13 (.in(_05_PXL));
  LED led_14 (.in(_04_PXL));
  LED led_15 (.in(_15_PXL));
  LED led_16 (.in(_14_PXL));
  LED led_17 (.in(_25_PXL));
  LED led_18 (.in(_24_PXL));
  LED led_19 (.in(_35_PXL));
  LED led_20 (.in(_34_PXL));
  LED led_21 (.in(_45_PXL));
  LED led_22 (.in(_44_PXL));
  LED led_23 (.in(_55_PXL));
  LED led_24 (.in(_54_PXL));
  LED led_25 (.in(_03_PXL));
  LED led_26 (.in(_02_PXL));
  LED led_27 (.in(_13_PXL));
  LED led_28 (.in(_12_PXL));
  LED led_29 (.in(_23_PXL));
  LED led_30 (.in(_22_PXL));
  LED led_31 (.in(_33_PXL));
  LED led_32 (.in(_32_PXL));
  LED led_33 (.in(_43_PXL));
  LED led_34 (.in(_42_PXL));
  LED led_35 (.in(_53_PXL));
  LED led_36 (.in(_52_PXL));
  LED led_37 (.in(_01_PXL));
  LED led_38 (.in(_00_PXL));
  LED led_39 (.in(_11_PXL));
  LED led_40 (.in(_10_PXL));
  LED led_41 (.in(_21_PXL));
  LED led_42 (.in(_20_PXL));
  LED led_43 (.in(_31_PXL));
  LED led_44 (.in(_30_PXL));
  LED led_45 (.in(_41_PXL));
  LED led_46 (.in(_40_PXL));
  LED led_47 (.in(_51_PXL));
  LED led_48 (.in(_50_PXL));
  Multiplexer multiplexer_1 (.sel(CLK_MODE), .in_0(clk), .in_1(CLK_2), .out(multiplexer_1_out));
  REGISTER_8 Address (.D(add_8_1_s), .E(1'b1), .CLK(multiplexer_1_out), .Q(Address_q));
  ADD_8 add_8_1 (.Cin(1'b0), .A(Address_q), .B(8'h1), .S(add_8_1_s));  // open: Cout
  ROM #(.AddrBits(8), .Bits(8)) DATA (.A(Address_q), .sel(1'b1), .D(DATA_d));
  ROM #(.AddrBits(8), .Bits(16)) INSTR (.A(Address_q), .sel(1'b1), .D(INSTR_d));
  CPU cpu_1 (
    .CLK(multiplexer_1_out), .IN({B7, B6, B5, B4, B3, B2, B1, B0, A7, A6, A5, A4, A3, A2, A1, A0}),
    .PROGRAM(PROGRAM), .IA(Address_q), .ID(INSTR_d), .DA(Address_q), .DD(DATA_d),
    .OUT({_57_PXL, _56_PXL, _55_PXL, _54_PXL, _53_PXL, _52_PXL, _51_PXL, _50_PXL, _47_PXL, _46_PXL, _45_PXL, _44_PXL, _43_PXL, _42_PXL, _41_PXL, _40_PXL, _37_PXL, _36_PXL, _35_PXL, _34_PXL, _33_PXL, _32_PXL, _31_PXL, _30_PXL, _27_PXL, _26_PXL, _25_PXL, _24_PXL, _23_PXL, _22_PXL, _21_PXL, _20_PXL, _17_PXL, _16_PXL, _15_PXL, _14_PXL, _13_PXL, _12_PXL, _11_PXL, _10_PXL, _07_PXL, _06_PXL, _05_PXL, _04_PXL, _03_PXL, _02_PXL, _01_PXL, _00_PXL}));

  // Notes on the sheet:
  //   clk: Hz: 25
  //   contents of DATA (hex, n*v repeats v):
  //   97,94,f6,94,97,4*44,77,30,48,48,48,30,44,45,55,6d,44,cf,29,2e
  //   ,2a,c9,47,44,44,44,77,20,a0,a0,80,20,213*0,ff,4*81,ff
  //   contents of INSTR (hex, n*v repeats v):
  //   ff10,10,1c18,1c38,1c58,1c78,3c18,3c38,c010,2010,1c08,2e,1c18,1c28
  //   ,2e,1c38,1c48,2e,1c58,1c68,2e,1c78,1c88,2e,3c18,7808,6cb4,60f2
  //   ,9c08,91e4,1e18,7828,6cb4,60f2,9c28,91e4,1e38,7848,6cb4,60f2,9c48
  //   ,91e4,1e58,7868,6cb4,60f2,9c68,91e4,1e78,7888,6cb4,60f2,9c88,91e4
  //   ,3e18,2022,4110,a50d,c0a2,43d0,8b6f,c010,12c
endmodule
