// Digital circuit CTRL_UNIT.dig as structural Verilog
module CTRL_UNIT (
  input  [15:0] INSTR,
  output [2:0] RSA1,
  output [2:0] RSA2,
  output [2:0] RDA,
  output RWE,
  output [2:0] ALOP,
  output OP2Sel,
  output [7:0] OP2Im,
  output [1:0] RDSrc
);

  wire and_1_out, and_2_out, and_3_out, nor_1_out;

  and and_1 (and_1_out, ~INSTR[0], INSTR[1]);  // And
  nor nor_1 (nor_1_out, INSTR[0], INSTR[1]);
  Multiplexer #(.Bits(3)) multiplexer_1 (.sel(and_1_out), .in_0(INSTR[12:10]), .in_1(INSTR[15:13]), .out(RSA1));
  and and_2 (and_2_out, nor_1_out, INSTR[2], ~INSTR[3]);  // And
  and and_3 (and_3_out, nor_1_out, ~INSTR[2], INSTR[3]);  // And
  assign ALOP = and_1_out ? INSTR[6:4] : 3'bz;  // Driver driver_1
  assign OP2Sel = and_2_out ? and_2_out : 1'bz;  // Driver driver_2
  assign ALOP = and_2_out ? INSTR[4:2] : 3'bz;  // Driver driver_3
  assign OP2Sel = and_3_out ? and_3_out : 1'bz;  // Driver driver_4
  assign RDSrc = and_3_out ? 2'b01 : 2'bz;  // Driver driver_5
  assign OP2Sel = and_1_out ? and_1_out : 1'bz;  // Driver driver_6
  PullDown #(.Bits(3)) pulldown_1 (.out(ALOP));
  PullDown pulldown_2 (.out(OP2Sel));
  PullDown pulldown_3 (.out(OP2Sel));
  PullDown #(.Bits(2)) pulldown_4 (.out(RDSrc));
  assign OP2Im = and_1_out ? INSTR[12:5] : 8'bz;  // Driver driver_7
  assign OP2Im = and_3_out ? {3'b000, INSTR[9:5]} : 8'bz;  // Driver driver_8
  PullDown #(.Bits(8)) pulldown_5 (.out(OP2Im));

  assign RDA = INSTR[15:13];
  assign RSA2 = INSTR[9:7];
  assign RWE = OP2Sel;

  // Notes on the sheet:
  //   Decode
  //   Branch Instr.
  //   ALU Imm. Instr.
  //   ALU Instr.
  //   Register Source /
  //   Destination Addresses
  //   Load Instr.
  //   Select RDA 
  //   as RSA2?
  //   2. Operand Select
  //   0 = RS2
  //   1 = Imm.
  //   ALU Operation
  //   Result Source
  //   Register Destination
  //   Write Enable
  //   Operand 2 Immediate
  //   Input
endmodule
